// Logisim project alu_top.circ as structural Verilog: 1 circuit, main circuit main
module main (
  input  [7:0] A_IN,
  input  [7:0] B_IN,
  input  GND,
  output [7:0] Output_bus_1,
  output [7:0] OVERALL,
  output [7:0] A_DEC,
  output [7:0] LSL,
  output [7:0] LSR,
  output [7:0] ASR,
  output [7:0] B_DEC,
  output [7:0] REV_A,
  output [7:0] LOGIC_OUT,
  output [7:0] SUM,
  output C_OUT,
  output LESS_FL,
  output EQUAL_FL,
  output GREAT_FL,
  output [7:0] CMP_REG,
  output M,
  output C_IN,
  output [1:0] B_SEL
);

  wire ADD, AND1, and_1_out, and_4_out, and_8_out, and_10_out, and_12_out, and_13_out, ASR1, clock_1_out,
       CMP1, CMP_NOT_SEL, DEC, INC, INVALID, LSL1, LSR1, NAND1, NOR1, not_1_out, not_2_out, not_3_out,
       not_4_out, not_5_out, not_6_out, not_7_out, not_8_out, not_9_out, not_10_out, not_11_out, not_12_out,
       not_13_out, not_14_out, not_15_out, not_16_out, not_17_out, not_18_out, not_19_out, not_20_out,
       not_21_out, not_22_out, not_24_out, not_25_out, not_26_out, not_27_out, not_28_out, not_29_out,
       not_30_out, not_31_out, not_32_out, not_33_out, not_34_out, not_35_out, not_36_out, not_37_out,
       not_38_out, not_39_out, not_40_out, not_41_out, NOT_A, NOT_B, OR1, or_3_out, or_6_out, PASS_A, PASS_B,
       REV_A1, SUB, XNOR1, XOR1;
  wire [1:0] or_5_out;
  wire [3:3] and_6_out, and_9_out, and_11_out;
  wire [4:0] CTRL;
  wire [7:0] bit_extender_1_out, bit_extender_2_out, LOGIC_SHIFT, multiplexer_1_out, multiplexer_2_out,
       multiplexer_3_out, nand_1_out, nor_2_out, NOT_A_B, RES_CMP_NOT, xor_1_out, xor_2_out;

  Counter #(.max('h1f), .width(5)) counter_1 (.clk(clock_1_out), .Q(CTRL));  // open: clr, load, up, count, D, carry
  Clock #(.phaseOffset(16)) clock_1 (.out(clock_1_out));
  not not_1 (not_1_out, CTRL[2]);
  and and_1 (and_1_out, not_1_out, CTRL[1]);
  and and_2 (B_SEL[0], and_1_out, CTRL[0]);
  and and_3 (B_SEL[1], and_1_out, not_2_out);
  not not_2 (not_2_out, CTRL[0]);
  or or_1 (C_IN, CTRL[1], M);
  not not_3 (not_3_out, CTRL[4]);
  not not_4 (not_4_out, CTRL[2]);
  and and_4 (and_4_out, not_4_out, CTRL[1]);
  and and_5 (B_SEL[0], and_4_out, CTRL[0]);
  and and_6 (and_6_out[3], not_3_out, CTRL[3]);
  not not_5 (not_5_out, CTRL[2]);
  not not_6 (not_6_out, CTRL[1]);
  not not_7 (not_7_out, CTRL[0]);
  and h_nand (NAND1, and_6_out[3], not_5_out, not_6_out, not_7_out);
  or or_2 (M, CTRL[4], CTRL[0]);
  not not_8 (not_8_out, CTRL[0]);
  and and_7 (B_SEL[1], and_4_out, not_8_out);
  not not_9 (not_9_out, CTRL[2]);
  not not_10 (not_10_out, CTRL[1]);
  not not_11 (not_11_out, CTRL[2]);
  and h_nor (NOR1, and_6_out[3], not_9_out, not_10_out, CTRL[0]);
  not not_12 (not_12_out, CTRL[0]);
  not not_13 (not_13_out, CTRL[2]);
  and h_xor (XOR1, and_6_out[3], not_11_out, CTRL[1], not_12_out);
  and h_a (PASS_A, and_6_out[3], not_13_out, CTRL[1], CTRL[0]);
  not not_14 (not_14_out, CTRL[1]);
  not not_15 (not_15_out, CTRL[0]);
  and h_b (PASS_B, and_6_out[3], CTRL[2], not_14_out, not_15_out);
  LED LED21 (.in(C_OUT));
  LED LED22 (.in(CMP_REG[0]));
  LED LED23 (.in(CMP_REG[1]));
  LED LED24 (.in(CMP_REG[2]));
  LED led_1 (.in(CMP_REG[1]));
  not not_16 (not_16_out, CTRL[1]);
  and h_and (AND1, and_6_out[3], CTRL[2], not_16_out, CTRL[0]);
  nor nor_1 (CMP_REG[1], SUM[7], SUM[6], SUM[5], SUM[4], SUM[3], SUM[2], SUM[1], SUM[0]);
  Multiplexer #(.select(2), .width(8)) multiplexer_1 (
    .in0(B_IN), .in1(8'h1), .in2({8{1'b0}}), .in3({8{1'b0}}), .out(multiplexer_1_out), .sel(B_SEL));
  assign bit_extender_1_out = {{7{M}}, M};  // Bit_Extender bit_extender_1
  not not_17 (not_17_out, CTRL[0]);
  and h_or (OR1, and_6_out[3], CTRL[2], CTRL[1], not_17_out);
  LED LED_1_dup2 (.in(ADD));
  LED LED_2 (.in(SUB));
  LED LED_3 (.in(INC));
  LED LED_4 (.in(DEC));
  LED LED_5 (.in(LSL1));
  LED LED_6 (.in(LSR1));
  LED LED_7 (.in(ASR1));
  LED LED_8 (.in(REV_A1));
  LED LED_9 (.in(NAND1));
  LED LED_10 (.in(NOR1));
  LED LED_20 (.in(INVALID));
  and h_xnor (XNOR1, and_6_out[3], CTRL[2], CTRL[1], CTRL[0]);
  assign nand_1_out = ~(A_IN & B_IN);  // NAND_Gate nand_1, 8 bits wide
  assign nor_2_out = ~(A_IN | B_IN);  // NOR_Gate nor_2, 8 bits wide
  assign xor_1_out = A_IN ^ B_IN;  // XOR_Gate xor_1, 8 bits wide
  assign xor_2_out = multiplexer_1_out ^ bit_extender_1_out;  // XOR_Gate xor_2, 8 bits wide
  LED LED_11 (.in(XOR1));
  LED LED_12 (.in(PASS_A));
  LED LED_13 (.in(PASS_B));
  LED LED_14 (.in(AND1));
  LED LED_15 (.in(OR1));
  LED LED_16 (.in(XNOR1));
  LED LED_17 (.in(CMP1));
  LED LED_18 (.in(NOT_A));
  LED LED_19 (.in(NOT_B));
  Adder adder_1 (.a(A_IN), .b(xor_2_out), .out(SUM), .cin(C_IN), .cout(C_OUT));
  Multiplexer #(.select(3), .width(8)) multiplexer_2 (
    .in0(nand_1_out), .in1(nor_2_out), .in2(xor_1_out), .in3(A_IN), .in4(B_IN), .in5(nand_1_out),
    .in6(nor_2_out), .in7(xor_1_out), .out(multiplexer_2_out), .sel(CTRL[2:0]));
  not not_18 (not_18_out, CTRL[2]);
  not not_19 (not_19_out, CTRL[1]);
  not not_20 (not_20_out, CTRL[0]);
  and h_add (ADD, and_9_out[3], not_18_out, not_19_out, not_20_out);
  Multiplexer #(.width(8)) multiplexer_3 (.in0(B_IN), .in1(A_IN), .out(multiplexer_3_out), .sel(CTRL[0]));
  not not_21 (not_21_out, CTRL[2]);
  not not_22 (not_22_out, CTRL[1]);
  and h_sub (SUB, and_9_out[3], not_21_out, not_22_out, CTRL[0]);
  assign bit_extender_2_out = {{7{and_8_out}}, and_8_out};  // Bit_Extender bit_extender_2
  and and_8 (and_8_out, CTRL[2], or_3_out);
  or or_3 (or_3_out, CTRL[1], CTRL[0]);
  assign NOT_A_B = ~multiplexer_3_out;  // NOT_Gate not_23, 8 bits wide
  not not_24 (not_24_out, CTRL[4]);
  not not_25 (not_25_out, CTRL[3]);
  and and_9 (and_9_out[3], not_24_out, not_25_out);
  not not_26 (not_26_out, CTRL[2]);
  not not_27 (not_27_out, CTRL[0]);
  and h_inc (INC, and_9_out[3], not_26_out, CTRL[1], not_27_out);
  nor nor_3 (CMP_REG[0], CMP_REG[1], C_OUT);
  not not_28 (not_28_out, CTRL[2]);
  and h_dec (DEC, and_9_out[3], not_28_out, CTRL[1], CTRL[0]);
  assign LOGIC_OUT = multiplexer_2_out ^ bit_extender_2_out;  // XOR_Gate xor_3, 8 bits wide
  not not_29 (not_29_out, CTRL[1]);
  not not_30 (not_30_out, CTRL[0]);
  not not_31 (not_31_out, CTRL[1]);
  and h_lsl (LSL1, and_9_out[3], CTRL[2], not_29_out, not_30_out);
  and h_lsr (LSR1, and_9_out[3], CTRL[2], not_31_out, CTRL[0]);
  nor nor_4 (CMP_REG[2], CMP_REG[1], CMP_REG[0]);
  not not_32 (not_32_out, CTRL[0]);
  and h_asr (ASR1, and_9_out[3], CTRL[2], CTRL[1], not_32_out);
  and h_rev_a (REV_A1, and_9_out[3], CTRL[2], CTRL[1], CTRL[0]);
  or or_4 (or_5_out[1], CTRL[4], CTRL[3]);
  not not_33 (not_33_out, CTRL[3]);
  and and_10 (and_10_out, CTRL[2], not_33_out);
  or or_5 (or_5_out[0], CTRL[4], and_10_out);
  not not_34 (not_34_out, CTRL[2]);
  not not_35 (not_35_out, CTRL[1]);
  not not_36 (not_36_out, CTRL[0]);
  and h_cmp (CMP1, and_11_out[3], not_34_out, not_35_out, not_36_out);
  not not_37 (not_37_out, CTRL[2]);
  not not_38 (not_38_out, CTRL[1]);
  and h_not_a (NOT_A, and_11_out[3], not_37_out, not_38_out, CTRL[0]);
  Multiplexer #(.select(2), .width(8)) multiplexer_4 (
    .in0(SUM), .in1(LOGIC_SHIFT), .in2(LOGIC_OUT), .in3(RES_CMP_NOT), .out(Output_bus_1), .sel(or_5_out));
  Multiplexer #(.select(2), .width(8)) multiplexer_5 (
    .in0({A_IN[6:0], GND}), .in1({GND, A_IN[7:1]}), .in2({{2{A_IN[7]}}, A_IN[6:1]}),
    .in3({A_IN[0], A_IN[1], A_IN[2], A_IN[3], A_IN[4], A_IN[5], A_IN[6], A_IN[7]}), .out(LOGIC_SHIFT),
    .sel(CTRL[1:0]));
  not not_39 (not_39_out, CTRL[3]);
  and and_11 (and_11_out[3], CTRL[4], not_39_out);
  not not_40 (not_40_out, CTRL[2]);
  not not_41 (not_41_out, CTRL[0]);
  and h_not_b (NOT_B, and_11_out[3], not_40_out, CTRL[1], not_41_out);
  Multiplexer #(.width(8)) multiplexer_6 (
    .in0({{5{GND}}, CMP_REG[2:0]}), .in1(NOT_A_B), .out(RES_CMP_NOT), .sel(CMP_NOT_SEL));
  or or_6 (or_6_out, CTRL[3], CTRL[2]);
  and and_12 (and_12_out, CTRL[4], or_6_out);
  or or_7 (CMP_NOT_SEL, CTRL[1], CTRL[0]);
  and and_13 (and_13_out, CTRL[4], CTRL[1], CTRL[0]);
  or or_8 (INVALID, and_12_out, and_13_out);

  assign A_DEC = A_IN;
  assign ASR = {{2{A_IN[7]}}, A_IN[6:1]};
  assign B_DEC = B_IN;
  assign CMP_REG[7:3] = {5{GND}};
  assign EQUAL_FL = CMP_REG[1];
  assign GREAT_FL = CMP_REG[2];
  assign LESS_FL = CMP_REG[0];
  assign LSL = {A_IN[6:0], GND};
  assign LSR = {GND, A_IN[7:1]};
  assign OVERALL = Output_bus_1;
  assign REV_A = {A_IN[0], A_IN[1], A_IN[2], A_IN[3], A_IN[4], A_IN[5], A_IN[6], A_IN[7]};

  // Other names for the same wires on the sheet: LOGIC_MUX_CTL[2:0] = CTRL[2:0]; A[7:0] = A_IN; B[7:0] = B_IN

  // Notes on the sheet:
  //   inputs
  //   outputs
endmodule
