// Logisim project alusimulation.circ as structural Verilog: 1 circuit, main circuit main
module main (
  input  [4:0] MainIn,
  input  [7:0] A_IN,
  input  [7:0] B_IN,
  input  GND,
  input  [7:0] cmp,
  output [7:0] OVERALL,
  output [7:0] out_7,
  output [7:0] LSL,
  output [7:0] LSR,
  output [7:0] ASR,
  output [7:0] out_11,
  output [7:0] REV_A,
  output [7:0] LOGIC_OUT,
  output M,
  output [7:0] SUM,
  output C_IN,
  output C_OUT,
  output [1:0] B_SEL,
  output LESS_FL,
  output EQUAL_FL,
  output GREAT_FL,
  output [7:0] CMP_REG
);

  wire and_1_out, and_5_out, and_8_out, CMP_NOT_SEL, h_a_out, h_add_out, h_and_out, h_asr_out, h_b_out,
       h_cmp_out, h_dec_out, h_inc_out, h_lsl_out, h_lsr_out, h_nand_out, h_nor_out, h_or_out, h_sub_out,
       h_xnor_out, h_xor_out, not_1_out, not_2_out, not_3_out, not_4_out, not_5_out, not_6_out, not_7_out,
       not_8_out, not_9_out, not_10_out, not_11_out, not_12_out, not_13_out, not_14_out, not_15_out,
       not_16_out, not_18_out, not_19_out, not_20_out, not_21_out, not_22_out, not_23_out, not_24_out,
       not_25_out, not_26_out, not_27_out, not_28_out, not_29_out, not_30_out, not_31_out, not_32_out,
       not_33_out, not_34_out, or_3_out;
  wire [1:0] or_5_out;
  wire [3:3] and_4_out, and_7_out;
  wire [7:0] bit_extender_1_out, bit_extender_2_out, LOGIC_SHIFT, multiplexer_1_out, multiplexer_2_out,
       multiplexer_3_out, nand_1_out, nor_2_out, NOT_A_B, RES_CMP_NOT, xor_1_out, xor_2_out;

  not not_1 (not_1_out, MainIn[3]);
  or or_1 (C_IN, not_1_out, MainIn[4]);
  not not_2 (not_2_out, MainIn[2]);
  and and_1 (and_1_out, not_2_out, MainIn[1]);
  and and_2 (B_SEL[0], and_1_out, MainIn[0]);
  or or_2 (M, MainIn[4], MainIn[0]);
  not not_3 (not_3_out, MainIn[0]);
  and and_3 (B_SEL[1], and_1_out, not_3_out);
  not not_4 (not_4_out, MainIn[4]);
  and and_4 (and_4_out[3], not_4_out, MainIn[3]);
  not not_5 (not_5_out, MainIn[2]);
  not not_6 (not_6_out, MainIn[1]);
  not not_7 (not_7_out, MainIn[0]);
  and h_nand (h_nand_out, and_4_out[3], not_5_out, not_6_out, not_7_out);
  LED LED_1 (.in(h_nand_out));
  not not_8 (not_8_out, MainIn[2]);
  not not_9 (not_9_out, MainIn[1]);
  and h_nor (h_nor_out, and_4_out[3], not_8_out, not_9_out, MainIn[0]);
  LED LED_2 (.in(h_nor_out));
  not not_10 (not_10_out, MainIn[2]);
  not not_11 (not_11_out, MainIn[0]);
  not not_12 (not_12_out, MainIn[2]);
  and h_xor (h_xor_out, and_4_out[3], not_10_out, MainIn[1], not_11_out);
  LED LED_3 (.in(h_xor_out));
  nor nor_1 (CMP_REG[1], SUM[7], SUM[6], SUM[5], SUM[4], SUM[3], SUM[2], SUM[1], SUM[0]);
  Multiplexer #(.select(2), .width(8)) multiplexer_1 (
    .in0(B_IN), .in1(8'h1), .in2({8{1'b0}}), .in3({8{1'b0}}), .out(multiplexer_1_out), .sel(B_SEL));
  assign bit_extender_1_out = {{7{M}}, M};  // Bit_Extender bit_extender_1
  not not_13 (not_13_out, MainIn[1]);
  and h_a (h_a_out, and_4_out[3], not_12_out, MainIn[1], MainIn[0]);
  and h_b (h_b_out, and_4_out[3], MainIn[2], not_13_out, not_15_out);
  LED LED_4 (.in(h_a_out));
  LED LED_5 (.in(h_b_out));
  not not_14 (not_14_out, MainIn[1]);
  not not_15 (not_15_out, MainIn[0]);
  and h_and (h_and_out, and_4_out[3], MainIn[2], not_14_out, MainIn[0]);
  LED LED_6 (.in(h_and_out));
  assign nand_1_out = ~(A_IN & B_IN);  // NAND_Gate nand_1, 8 bits wide
  assign nor_2_out = ~(A_IN | B_IN);  // NOR_Gate nor_2, 8 bits wide
  assign xor_1_out = A_IN ^ B_IN;  // XOR_Gate xor_1, 8 bits wide
  not not_16 (not_16_out, MainIn[0]);
  and h_or (h_or_out, and_4_out[3], MainIn[2], MainIn[1], not_16_out);
  LED LED_7 (.in(h_or_out));
  assign xor_2_out = multiplexer_1_out ^ bit_extender_1_out;  // XOR_Gate xor_2, 8 bits wide
  and h_xnor (h_xnor_out, and_4_out[3], MainIn[2], MainIn[1], MainIn[0]);
  LED LED_8 (.in(h_xnor_out));
  Adder adder_1 (.a(A_IN), .b(xor_2_out), .out(SUM), .cin(C_IN), .cout(C_OUT));
  Multiplexer #(.select(3), .width(8)) multiplexer_2 (
    .in0(nand_1_out), .in1(nor_2_out), .in2(xor_1_out), .in3(A_IN), .in4(B_IN), .in5(nand_1_out),
    .in6(nor_2_out), .in7(xor_1_out), .out(multiplexer_2_out), .sel(MainIn[2:0]));
  Multiplexer #(.width(8)) multiplexer_3 (.in0(B_IN), .in1(A_IN), .out(multiplexer_3_out), .sel(MainIn[0]));
  assign bit_extender_2_out = {{7{and_5_out}}, and_5_out};  // Bit_Extender bit_extender_2
  and and_5 (and_5_out, MainIn[2], or_3_out);
  or or_3 (or_3_out, MainIn[1], MainIn[0]);
  assign NOT_A_B = ~multiplexer_3_out;  // NOT_Gate not_17, 8 bits wide
  not not_18 (not_18_out, MainIn[2]);
  not not_19 (not_19_out, MainIn[1]);
  not not_20 (not_20_out, MainIn[0]);
  and h_add (h_add_out, and_7_out[3], not_18_out, not_19_out, not_20_out);
  LED LED_9 (.in(h_add_out));
  and and_6 (CMP_REG[2], not_22_out, not_21_out);
  not not_21 (not_21_out, CMP_REG[0]);
  not not_22 (not_22_out, CMP_REG[1]);
  nor nor_3 (CMP_REG[0], CMP_REG[1], C_OUT);
  not not_23 (not_23_out, MainIn[2]);
  not not_24 (not_24_out, MainIn[1]);
  and h_sub (h_sub_out, and_7_out[3], not_23_out, not_24_out, MainIn[0]);
  LED led_1_dup2 (.in(h_sub_out));
  assign LOGIC_OUT = multiplexer_2_out ^ bit_extender_2_out;  // XOR_Gate xor_3, 8 bits wide
  not not_25 (not_25_out, MainIn[4]);
  not not_26 (not_26_out, MainIn[3]);
  and and_7 (and_7_out[3], not_25_out, not_26_out);
  not not_27 (not_27_out, MainIn[2]);
  not not_28 (not_28_out, MainIn[0]);
  and h_inc (h_inc_out, and_7_out[3], not_27_out, MainIn[1], not_28_out);
  LED led_2_dup2 (.in(h_inc_out));
  not not_29 (not_29_out, MainIn[2]);
  and h_dec (h_dec_out, and_7_out[3], not_29_out, MainIn[1], MainIn[0]);
  LED led_3_dup2 (.in(h_dec_out));
  not not_30 (not_30_out, MainIn[1]);
  not not_31 (not_31_out, MainIn[0]);
  and h_lsl (h_lsl_out, and_7_out[3], MainIn[2], not_30_out, not_31_out);
  LED led_4_dup2 (.in(h_lsl_out));
  or or_4 (or_5_out[1], MainIn[4], MainIn[3]);
  not not_32 (not_32_out, MainIn[1]);
  and h_lsr (h_lsr_out, and_7_out[3], MainIn[2], not_32_out, MainIn[0]);
  and h_asr (h_asr_out, and_7_out[3], MainIn[2], MainIn[1], not_34_out);
  LED led_5_dup2 (.in(h_lsr_out));
  LED led_6_dup2 (.in(h_asr_out));
  not not_33 (not_33_out, MainIn[3]);
  and and_8 (and_8_out, MainIn[2], not_33_out);
  or or_5 (or_5_out[0], MainIn[4], and_8_out);
  not not_34 (not_34_out, MainIn[0]);
  and h_cmp (h_cmp_out, and_7_out[3], MainIn[2], MainIn[1], MainIn[0]);
  LED led_7_dup2 (.in(h_cmp_out));
  Multiplexer #(.select(2), .width(8)) multiplexer_4 (
    .in0(SUM), .in1(LOGIC_SHIFT), .in2(LOGIC_OUT), .in3(RES_CMP_NOT), .out(OVERALL), .sel(or_5_out));
  Multiplexer #(.select(2), .width(8)) multiplexer_5 (
    .in0({A_IN[6:0], GND}), .in1({GND, A_IN[7:1]}), .in2({{2{A_IN[7]}}, A_IN[6:1]}),
    .in3({A_IN[0], A_IN[1], A_IN[2], A_IN[3], A_IN[4], A_IN[5], A_IN[6], A_IN[7]}), .out(LOGIC_SHIFT),
    .sel(MainIn[1:0]));
  Multiplexer #(.width(8)) multiplexer_6 (.in0(cmp), .in1(NOT_A_B), .out(RES_CMP_NOT), .sel(CMP_NOT_SEL));
  or or_6 (CMP_NOT_SEL, MainIn[1], MainIn[0]);

  assign ASR = {{2{A_IN[7]}}, A_IN[6:1]};
  assign CMP_REG[7:3] = {5{GND}};
  assign EQUAL_FL = CMP_REG[1];
  assign GREAT_FL = CMP_REG[2];
  assign LESS_FL = CMP_REG[0];
  assign LSL = {A_IN[6:0], GND};
  assign LSR = {GND, A_IN[7:1]};
  assign out_7 = A_IN;
  assign out_11 = B_IN;
  assign REV_A = {A_IN[0], A_IN[1], A_IN[2], A_IN[3], A_IN[4], A_IN[5], A_IN[6], A_IN[7]};

  // Other names for the same wires on the sheet: CTRL[4:0] = MainIn; LOGIC_MUX_CTL[2:0] = MainIn[2:0]; A[7:0] = A_IN;
  //   B[7:0] = B_IN

  // Notes on the sheet:
  //   inputs
  //   outputs
endmodule
